// Logisim project Clock.circ as structural Verilog
module clock (
);

  Hex_Digit_Display hex_digit_display_1 (.dp(1'b0));  // open: value
  Hex_Digit_Display hex_digit_display_2 (.dp(1'b0));  // open: value
  Hex_Digit_Display hex_digit_display_3 (.dp(1'b0));  // open: value
  Hex_Digit_Display hex_digit_display_4 (.dp(1'b0));  // open: value
endmodule

module proxEstado9 (
  input  a,
  input  b,
  input  c,
  input  d,
  output sa,
  output sb,
  output sc,
  output sd
);

  wire and_1_out, and_2_out, and_3_out, and_4_out, and_5_out, and_6_out, and_7_out, not_1_out, not_2_out,
       not_3_out, not_4_out, not_5_out, not_6_out, not_7_out;

  and and_1 (and_1_out, b, c, d);
  and and_2 (and_2_out, a, not_1_out);
  not not_1 (not_1_out, d);
  not not_2 (not_2_out, b);
  and and_3 (and_3_out, not_2_out, c, d);
  and and_4 (and_4_out, b, not_3_out);
  not not_3 (not_3_out, c);
  and and_5 (and_5_out, b, not_4_out);
  not not_4 (not_4_out, d);
  not not_5 (not_5_out, a);
  not not_6 (not_6_out, c);
  and and_6 (and_6_out, not_5_out, not_6_out, d);
  and and_7 (and_7_out, c, not_7_out);
  not not_7 (not_7_out, d);
  not not_8 (sd, d);
  or or_1 (sa, and_1_out, and_2_out);
  or or_2 (sb, and_3_out, and_4_out, and_5_out);
  or or_3 (sc, and_6_out, and_7_out);
endmodule

module proxEstado5 (
  input  a,
  input  b,
  input  c,
  output sa,
  output sb,
  output sc
);

  wire and_1_out, and_2_out, and_3_out, and_4_out, not_1_out, not_2_out, not_3_out, not_4_out;

  not not_1 (not_1_out, c);
  not not_2 (not_2_out, a);
  not not_3 (not_3_out, b);
  not not_4 (not_4_out, c);
  not not_5 (sc, c);
  and and_1 (and_1_out, b, c);
  and and_2 (and_2_out, a, not_1_out);
  and and_3 (and_3_out, not_2_out, not_3_out, c);
  and and_4 (and_4_out, b, not_4_out);
  or or_1 (sa, and_1_out, and_2_out);
  or or_2 (sb, and_3_out, and_4_out);
endmodule

module clock5 (
);

  wire clock_1_out, proxestado5_1_sa, proxestado5_1_sb, proxestado5_1_sc;
  wire [2:0] d_ff_3_q;

  Clock clock_1 (.out(clock_1_out));
  D_Flip_Flop d_ff_1 (.clk(clock_1_out), .D(proxestado5_1_sa), .Q(d_ff_3_q[2]));  // open: Qn, preset, en, reset
  proxEstado5 proxestado5_1 (
    .a(d_ff_3_q[2]), .b(d_ff_3_q[1]), .c(d_ff_3_q[0]), .sa(proxestado5_1_sa), .sb(proxestado5_1_sb),
    .sc(proxestado5_1_sc));
  D_Flip_Flop d_ff_2 (.clk(clock_1_out), .D(proxestado5_1_sb), .Q(d_ff_3_q[1]));  // open: Qn, preset, en, reset
  D_Flip_Flop d_ff_3 (.clk(clock_1_out), .D(proxestado5_1_sc), .Q(d_ff_3_q[0]));  // open: Qn, preset, en, reset
  Hex_Digit_Display hex_digit_display_1 (.value({1'b0, d_ff_3_q}), .dp(1'b0));
endmodule

module clock9 (
);

  wire clock_1_out, proxestado9_1_sa, proxestado9_1_sb, proxestado9_1_sc, proxestado9_1_sd;
  wire [3:0] d_ff_4_q;

  Clock clock_1 (.out(clock_1_out));
  D_Flip_Flop d_ff_1 (.clk(clock_1_out), .D(proxestado9_1_sa), .Q(d_ff_4_q[3]));  // open: Qn, preset, en, reset
  proxEstado9 proxestado9_1 (
    .a(d_ff_4_q[3]), .b(d_ff_4_q[2]), .c(d_ff_4_q[1]), .d(d_ff_4_q[0]), .sa(proxestado9_1_sa),
    .sb(proxestado9_1_sb), .sc(proxestado9_1_sc), .sd(proxestado9_1_sd));
  D_Flip_Flop d_ff_2 (.clk(clock_1_out), .D(proxestado9_1_sb), .Q(d_ff_4_q[2]));  // open: Qn, preset, en, reset
  D_Flip_Flop d_ff_3 (.clk(clock_1_out), .D(proxestado9_1_sc), .Q(d_ff_4_q[1]));  // open: Qn, preset, en, reset
  D_Flip_Flop d_ff_4 (.clk(clock_1_out), .D(proxestado9_1_sd), .Q(d_ff_4_q[0]));  // open: Qn, preset, en, reset
  Hex_Digit_Display hex_digit_display_1 (.value(d_ff_4_q), .dp(1'b0));
endmodule
